// Digital circuit 10.dig as structural Verilog
module _10 (
  input  [8:0] N,
  input  reset,
  input  start,
  input  clock,
  output done,
  output [7:0] displayout,
  output [15:0] clockcount,
  output valid
);

  wire comparator_1_lt, comparator_2_lt, comparator_3_gt, multiplexer_10_out, multiplexer_11_out,
       multiplexer_14_out, not_1_out, not_2_out, or_1_out, s0, s1, s2, s3, s4, s5, s6, s7;
  wire [2:0] multiplexer_2_out, multiplexer_3_out, state, state_q, stateFrom0, stateFrom1, stateFrom4,
       stateFrom5;
  wire [7:0] multiplexer_9_out, ROMout;
  wire [8:0] add_1_s, add_3_s, add_4_s, count, index, multiplexer_8_out, multiplexer_12_out,
       multiplexer_13_out, multiplexer_16_out, RAMout, sub_1_s, temp;
  wire [15:0] add_2_s, multiplexer_15_out;

  Comparator #(.Bits(9)) comparator_1 (.a(index), .b(N), .lt(comparator_1_lt));  // open: gt, eq
  Multiplexer #(.Bits(3), .Selector_Bits(3)) multiplexer_1 (
    .sel(state_q), .in_0(stateFrom0), .in_1(stateFrom1), .in_2(3'b001), .in_3(3'b100), .in_4(stateFrom4),
    .in_5(stateFrom5), .in_6(3'b101), .in_7(3'b111), .out(state));
  D_FF #(.Bits(3)) u_state (.D(state), .C(clock), .Q(state_q));  // open: nQ
  Multiplexer #(.Bits(3)) multiplexer_2 (.sel(not_1_out), .in_0(3'b010), .in_1(3'b011), .out(multiplexer_2_out));
  not not_1 (not_1_out, comparator_1_lt);
  Multiplexer #(.Bits(3)) multiplexer_3 (.sel(reset), .in_0(3'b101), .in_1(3'b000), .out(multiplexer_3_out));
  Comparator #(.Bits(9)) comparator_2 (.a(count), .b(9'hff), .lt(comparator_2_lt));  // open: gt, eq
  Comparator #(.Bits(9)) comparator_3 (.a(count), .b({9{1'b0}}), .gt(comparator_3_gt));  // open: eq, lt
  Multiplexer #(.Bits(3)) multiplexer_4 (.sel(start), .in_0(3'b000), .in_1(3'b001), .out(stateFrom0));
  Multiplexer #(.Bits(3)) multiplexer_5 (.sel(reset), .in_0(multiplexer_2_out), .in_1(3'b000), .out(stateFrom1));
  Multiplexer #(.Bits(3)) multiplexer_6 (.sel(not_2_out), .in_0(multiplexer_3_out), .in_1(3'b111), .out(stateFrom4));
  not not_2 (not_2_out, comparator_2_lt);
  Multiplexer #(.Bits(3)) multiplexer_7 (.sel(comparator_3_gt), .in_0(3'b100), .in_1(3'b110), .out(stateFrom5));
  Decoder #(.Selector_Bits(3)) decoder_1 (
    .sel(state), .out_0(s0), .out_1(s1), .out_2(s2), .out_3(s3), .out_4(s4), .out_5(s5), .out_6(s6),
    .out_7(s7));
  Add #(.Bits(9)) add_1 (.a(index), .b({9{1'b0}}), .c_i(1'b1), .s(add_1_s));  // open: c_o
  Sub #(.Bits(9)) sub_1 (.a(count), .b(9'h1), .c_i(1'b0), .s(sub_1_s));  // open: c_o
  Multiplexer #(.Selector_Bits(3), .Bits(9)) multiplexer_8 (
    .sel(state), .in_0({9{1'b0}}), .in_1(index), .in_2(add_1_s), .in_3({9{1'b1}}), .in_4(add_1_s),
    .in_5(index), .in_6(index), .in_7(index), .out(multiplexer_8_out));
  Multiplexer #(.Selector_Bits(3), .Bits(8)) multiplexer_9 (
    .sel(state), .in_0({8{1'b0}}), .in_1(displayout), .in_2(displayout), .in_3(displayout),
    .in_4(displayout), .in_5(displayout), .in_6(index[7:0]), .in_7(displayout), .out(multiplexer_9_out));
  Multiplexer #(.Selector_Bits(3)) multiplexer_10 (
    .sel(state), .in_0(1'b0), .in_1(valid), .in_2(valid), .in_3(valid), .in_4(1'b0), .in_5(valid),
    .in_6(1'b1), .in_7(valid), .out(multiplexer_10_out));
  Multiplexer #(.Selector_Bits(3)) multiplexer_11 (
    .sel(state), .in_0(1'b0), .in_1(done), .in_2(done), .in_3(done), .in_4(done), .in_5(done), .in_6(done),
    .in_7(1'b1), .out(multiplexer_11_out));
  Multiplexer #(.Bits(9)) multiplexer_12 (.sel(or_1_out), .in_0(temp), .in_1(RAMout), .out(multiplexer_12_out));
  Multiplexer #(.Selector_Bits(3), .Bits(9)) multiplexer_13 (
    .sel(state), .in_0({9{1'b0}}), .in_1(count), .in_2(count), .in_3(count), .in_4(RAMout), .in_5(count),
    .in_6(sub_1_s), .in_7(count), .out(multiplexer_13_out));
  D_FF #(.Bits(9)) u_index (.D(multiplexer_8_out), .C(clock), .Q(index));  // open: nQ
  D_FF #(.Bits(8)) u_displayout (.D(multiplexer_9_out), .C(clock), .Q(displayout));  // open: nQ
  D_FF u_valid (.D(multiplexer_10_out), .C(clock), .Q(valid));  // open: nQ
  D_FF u_done (.D(multiplexer_11_out), .C(clock), .Q(done));  // open: nQ
  D_FF #(.Bits(9)) u_temp (.D(multiplexer_12_out), .C(clock), .Q(temp));  // open: nQ
  D_FF #(.Bits(9)) u_count (.D(multiplexer_13_out), .C(clock), .Q(count));  // open: nQ
  Multiplexer multiplexer_14 (.sel(done), .in_0(start), .in_1(1'b0), .out(multiplexer_14_out));
  Seven_Seg_Hex seven_seg_hex_1 (.d(displayout[7:4]), .dp(1'b0));
  Multiplexer #(.Bits(16)) multiplexer_15 (.sel(reset), .in_0(clockcount), .in_1({16{1'b0}}), .out(multiplexer_15_out));
  Seven_Seg_Hex seven_seg_hex_2 (.d(displayout[3:0]), .dp(1'b0));
  Add #(.Bits(16)) add_2 (.a(multiplexer_15_out), .b({16{1'b0}}), .c_i(multiplexer_14_out), .s(add_2_s));  // open: c_o
  Add #(.Bits(9)) add_3 (.a(index), .b({9{1'b0}}), .c_i(1'b1), .s(add_3_s));  // open: c_o
  Multiplexer #(.Bits(9)) multiplexer_16 (.sel(s4), .in_0({1'b0, ROMout}), .in_1(add_3_s), .out(multiplexer_16_out));
  Add #(.Bits(9)) add_4 (.a(temp), .b({9{1'b0}}), .c_i(1'b1), .s(add_4_s));  // open: c_o
  D_FF #(.Bits(16)) d_ff_1 (.D(add_2_s), .C(clock), .Q(clockcount));  // open: nQ
  or or_1 (or_1_out, s1, s4);
  ROM #(.AddrBits(9), .isProgramMemory("true"), .Bits(8)) ROMFILE (.A(index), .sel(1'b1), .D(ROMout));
  RAMDualPort #(.AddrBits(9), .Bits(9)) RAM (
    .A(multiplexer_16_out), .Din(add_4_s), .str(s2), .C(clock), .ld(or_1_out), .D(RAMout));

  // Notes on the sheet:
  //   contents of ROMFILE (hex, n*v repeats v):
  //   1,4,2,3
endmodule
